// Logisim project ALU.circ as structural Verilog
module ALU (
  input  [15:0] in_1,
  input  [15:0] in_2,
  input  [1:0] in_3,
  output out_4,
  output [15:0] out_5
);

  wire [15:0] and_1_out, multiplier_1_out, nor_1_out, subtractor_1_out;

  assign and_1_out = in_1 & in_2;  // AND_Gate and_1, 16 bits wide
  assign nor_1_out = ~(in_1 | in_2);  // NOR_Gate nor_1, 16 bits wide
  Subtractor #(.width(16)) subtractor_1 (.a(in_1), .b(in_2), .out(subtractor_1_out));  // open: bin, bout
  Multiplier #(.width(16)) multiplier_1 (.a(in_1), .b(in_2), .out(multiplier_1_out));  // open: cin, cout
  Multiplexer #(.select(2), .width(16), .enable("false")) multiplexer_1 (
    .in0(and_1_out), .in1(nor_1_out), .in2(subtractor_1_out), .in3(multiplier_1_out),
    .out({out_4, out_5[14:0]}), .sel(in_3));

  assign out_5[15] = out_4;
endmodule

module CPU (
);

  wire alu_1_p1, alu_1_p2;
  wire [19:0] rom_1_data;

  Register #(.width(16)) PC ();  // open: D, en, Q, clk, clr
  ROM #(.addrWidth(16), .dataWidth(20)) rom_1 (.data(rom_1_data));  // open: addr, sel
  // ALU alu_1: pin names not known; wires that end beside it: alu_1_p1, alu_1_p2, alu_1_p1, alu_1_p2
endmodule

module ControlUnit (
  input  [3:0] in_1,
  output slt,
  output ALUsrc,
  output REGwrite,
  output jump,
  output regDst,
  output ra,
  output [1:0] ALUcnt
);

  wire and_out, andi_out, mul_out, nor_out, sll_out, slt_out, slti_out;

  and \nor  (nor_out, ~in_1[3], ~in_1[2], ~in_1[1], ~in_1[0]);  // AND_Gate
  and u_slt (slt_out, ~in_1[3], in_1[2], ~in_1[1], in_1[0]);  // AND_Gate
  and sll (sll_out, ~in_1[3], ~in_1[2], ~in_1[1], in_1[0]);  // AND_Gate
  and slti (slti_out, ~in_1[3], ~in_1[2], in_1[1], ~in_1[0]);  // AND_Gate
  and andi (andi_out, ~in_1[3], in_1[2], ~in_1[1], ~in_1[0]);  // AND_Gate
  and \and  (and_out, ~in_1[3], in_1[2], in_1[1], in_1[0]);  // AND_Gate
  and mul (mul_out, in_1[3], in_1[2], in_1[1], in_1[0]);
  and jal (jump, in_1[3], ~in_1[2], in_1[1], in_1[0]);  // AND_Gate
  or or_1 (ALUcnt[1], mul_out, slt_out, slti_out);
  or or_2 (ALUcnt[0], mul_out, nor_out);
  or or_3 (slt, slt_out, slti_out);
  or or_4 (ALUsrc, andi_out, slti_out);
  or or_5 (REGwrite, jump, mul_out, andi_out, and_out, slti_out, sll_out, slt_out, nor_out);
  or or_6 (regDst, andi_out, slti_out);

  assign ra = jump;
endmodule
